// Logisim project LC-3-v2.circ as structural Verilog: 15 circuits, main circuit main
// RES
module main (
  input  Reset,
  output out_2,
  output out_3,
  output out_4,
  output out_5,
  output out_6,
  output out_7,
  output out_8,
  output [15:0] out_9,
  output [15:0] out_10,
  output [15:0] out_11,
  output [15:0] out_12,
  output [15:0] out_13,
  output [15:0] out_14,
  output [15:0] out_15,
  output [15:0] out_16,
  output [15:0] out_17,
  output halt,
  output [15:0] out_19,
  output [15:0] out_20,
  output [15:0] out_21,
  output [15:0] out_22
);

  wire decodeir_1_writereg, getcst_1_usecst, or16_1_out_2, or16_2_out_2, ramctrl_1_memload,
       ramctrl_1_memstore;
  wire [2:0] nzp_1_nzp;
  wire [15:0] alu_1_output, getcst_1_cst, RegIN, registres_1_out_sr1, registres_1_out_sr2;

  BiClock biclock_1 (.reset(Reset), .signal0(out_2), .signal1(out_3));
  RegPC regpc_1 (
    .H(out_3), .PC(out_9), .Reset(Reset), .IR(out_10), .R(registres_1_out_sr1), .TestNZP(out_5), .Jump(out_4));
  // Probe on out_9
  // Probe on out_11
  GetAddr getaddr_1 (.PC(out_9), .BaseR(registres_1_out_sr1), .IR(out_10), .Addr(out_11), .Fetch(out_2));
  // Probe on out_12
  LED led_1 (.in(out_6));
  RamCtrl ramctrl_1 (
    .Store(out_7), .Fetch(out_2), .Exec(out_3), .Load(out_6), .MemStore(ramctrl_1_memstore),
    .MemLoad(ramctrl_1_memload));
  LED led_2 (.in(out_7));
  // Probe on out_13
  RAM #(.addrWidth(16), .dataWidth(16), .bus("separate")) ram_1 (
    .addr(out_11), .din(out_12), .data(out_13), .str(ramctrl_1_memstore), .clk(ramctrl_1_memstore),
    .ld(ramctrl_1_memload));  // open: sel, clr
  Register #(.width(16), .trigger("falling")) RegIR (.D(out_13), .Q(out_10), .clk(out_2));  // open: en, clr
  DecodeIR decodeir_1 (.IR(out_10), .Jump(out_4), .WriteReg(decodeir_1_writereg), .Load(out_6), .Store(out_7));
  // Probe on out_10[11:9]
  // Probe on out_10[8:6]
  // Probe on out_10[2:0]
  // Probe on getcst_1_cst
  GetCst getcst_1 (.IR(out_10), .Cst(getcst_1_cst), .UseCst(getcst_1_usecst));
  // Probe on out_10[15:14]
  and and_1 (out_8, decodeir_1_writereg, out_3);
  Registres registres_1 (
    .SR1(out_10[8:6]), .IN(RegIN), .SR2(out_10[2:0]), .WriteReg(out_8), .DR_SR(out_10[11:9]),
    .OUT_SR1(registres_1_out_sr1), .OUT_SR2(registres_1_out_sr2), .OUT_SR(out_12), .R0(out_14), .R1(out_15),
    .R2(out_16), .R3(out_17), .R4(out_19), .R5(out_20), .R6(out_21), .R7(out_22));
  // Probe on registres_1_out_sr1
  ALU alu_1 (
    .UseCst(getcst_1_usecst), .e2(out_10[15:14]), .Input1(registres_1_out_sr1), .Input2(registres_1_out_sr2),
    .Cst(getcst_1_cst), .Output(alu_1_output));
  // Probe on registres_1_out_sr2
  // Probe on alu_1_output
  NZP nzp_1 (.RES(RegIN), .NZP(nzp_1_nzp), .IR(out_10), .TestNZP(out_5), .WriteReg(out_8));
  // Probe on nzp_1_nzp
  Or16 or16_1 (.in_1(out_10), .out_2(or16_1_out_2));
  Or16 or16_2 (.in_1(out_9), .out_2(or16_2_out_2));
  // Probe on out_14
  // Probe on out_15
  // Probe on out_16
  // Probe on out_17
  // Probe on out_19
  // Probe on out_20
  // Probe on out_21
  // Probe on out_22
  and and_2 (halt, ~or16_1_out_2, or16_2_out_2);  // AND_Gate
  WriteVal writeval_1 (
    .Load(out_6), .ALURes(alu_1_output), .MemOUT(out_13), .IR(out_10), .PC(out_9), .RegIN(RegIN));  // open: Off9

  // Other names for the same wires on the sheet: Addr[15:0] = out_11; Condition = out_5; Exec = out_3; Fetch = out_2;
  //   IR[15:0] = out_10; JumpInstr = out_4; Load = out_6; MemIN[15:0] = out_12; MemOUT[15:0] = out_13;
  //   PC[15:0] = out_9; R0[15:0] = out_14; R1[15:0] = out_15; R2[15:0] = out_16; R3[15:0] = out_17; R4[15:0] = out_19;
  //   R5[15:0] = out_20; R6[15:0] = out_21; R7[15:0] = out_22; Store = out_7; WriteReg = out_8

  // Notes on the sheet:
  //   R
  //   IR
  //   R
  //   IR
  //   RAM
  //   Traces (NE PAS MODIFIER)______________________________________________________________________________________________________
  //   GetOp
  //   Arret des traces au 1er NOP
endmodule

module ALU (
  input  [15:0] Input1,
  input  [15:0] Input2,
  input  [15:0] Cst,
  input  UseCst,
  input  [1:0] e2,
  output [15:0] Output
);

  wire [4:0] adder_2_out, adder_3_out, adder_4_out, adder_5_out, adder_6_out, adder_7_out, adder_8_out,
       adder_9_out, adder_10_out, adder_11_out, adder_12_out, adder_13_out, adder_14_out, adder_15_out,
       adder_16_out, bit_extender_1_out, bit_extender_2_out, bit_extender_3_out, bit_extender_4_out,
       bit_extender_5_out, bit_extender_6_out, bit_extender_7_out, bit_extender_8_out, bit_extender_9_out,
       bit_extender_10_out, bit_extender_11_out, bit_extender_12_out, bit_extender_13_out,
       bit_extender_14_out, bit_extender_15_out, bit_extender_16_out;
  wire [15:0] adder_1_out, and_1_out, bit_extender_17_out, multiplexer_1_out, xor_1_out;

  assign bit_extender_1_out = {{4{1'b0}}, Input1[0]};  // Bit_Extender bit_extender_1
  assign bit_extender_2_out = {{4{1'b0}}, Input1[1]};  // Bit_Extender bit_extender_2
  assign bit_extender_3_out = {{4{1'b0}}, Input1[2]};  // Bit_Extender bit_extender_3
  assign bit_extender_4_out = {{4{1'b0}}, Input1[3]};  // Bit_Extender bit_extender_4
  assign bit_extender_5_out = {{4{1'b0}}, Input1[4]};  // Bit_Extender bit_extender_5
  assign bit_extender_6_out = {{4{1'b0}}, Input1[5]};  // Bit_Extender bit_extender_6
  assign bit_extender_7_out = {{4{1'b0}}, Input1[6]};  // Bit_Extender bit_extender_7
  assign bit_extender_8_out = {{4{1'b0}}, Input1[7]};  // Bit_Extender bit_extender_8
  assign bit_extender_9_out = {{4{1'b0}}, Input1[8]};  // Bit_Extender bit_extender_9
  assign bit_extender_10_out = {{4{1'b0}}, Input1[9]};  // Bit_Extender bit_extender_10
  assign bit_extender_11_out = {{4{1'b0}}, Input1[10]};  // Bit_Extender bit_extender_11
  assign bit_extender_12_out = {{4{1'b0}}, Input1[11]};  // Bit_Extender bit_extender_12
  assign bit_extender_13_out = {{4{1'b0}}, Input1[12]};  // Bit_Extender bit_extender_13
  assign bit_extender_14_out = {{4{1'b0}}, Input1[13]};  // Bit_Extender bit_extender_14
  assign bit_extender_15_out = {{4{1'b0}}, Input1[14]};  // Bit_Extender bit_extender_15
  assign bit_extender_16_out = {{4{1'b0}}, Input1[15]};  // Bit_Extender bit_extender_16
  Multiplexer #(.width(16), .enable("false")) multiplexer_1 (
    .in0(Input2), .in1(Cst), .out(multiplexer_1_out), .sel(UseCst));
  Adder #(.width(16)) adder_1 (.a(multiplexer_1_out), .b(Input1), .out(adder_1_out));  // open: cin, cout
  Adder #(.width(5)) adder_2 (.a(bit_extender_1_out), .b(bit_extender_2_out), .out(adder_2_out));  // open: cin, cout
  Adder #(.width(5)) adder_3 (.a(bit_extender_3_out), .b(bit_extender_4_out), .out(adder_3_out));  // open: cin, cout
  Adder #(.width(5)) adder_4 (.a(bit_extender_5_out), .b(bit_extender_6_out), .out(adder_4_out));  // open: cin, cout
  Adder #(.width(5)) adder_5 (.a(bit_extender_7_out), .b(bit_extender_8_out), .out(adder_5_out));  // open: cin, cout
  Adder #(.width(5)) adder_6 (.a(bit_extender_9_out), .b(bit_extender_10_out), .out(adder_6_out));  // open: cin, cout
  Adder #(.width(5)) adder_7 (.a(bit_extender_11_out), .b(bit_extender_12_out), .out(adder_7_out));  // open: cin, cout
  Adder #(.width(5)) adder_8 (.a(bit_extender_13_out), .b(bit_extender_14_out), .out(adder_8_out));  // open: cin, cout
  Adder #(.width(5)) adder_9 (.a(bit_extender_15_out), .b(bit_extender_16_out), .out(adder_9_out));  // open: cin, cout
  assign and_1_out = Input1 & multiplexer_1_out;  // AND_Gate and_1, 16 bits wide
  Multiplexer #(.select(2), .width(16), .enable("false")) multiplexer_2 (
    .in0(adder_1_out), .in1(and_1_out), .in2(xor_1_out), .in3({16{1'b1}}), .out(Output), .sel(e2));
  Adder #(.width(5)) adder_10 (.a(adder_2_out), .b(adder_3_out), .out(adder_10_out));  // open: cin, cout
  Adder #(.width(5)) adder_11 (.a(adder_4_out), .b(adder_5_out), .out(adder_11_out));  // open: cin, cout
  Adder #(.width(5)) adder_12 (.a(adder_6_out), .b(adder_7_out), .out(adder_12_out));  // open: cin, cout
  Adder #(.width(5)) adder_13 (.a(adder_8_out), .b(adder_9_out), .out(adder_13_out));  // open: cin, cout
  Adder #(.width(5)) adder_14 (.a(adder_10_out), .b(adder_11_out), .out(adder_14_out));  // open: cin, cout
  Adder #(.width(5)) adder_15 (.a(adder_12_out), .b(adder_13_out), .out(adder_15_out));  // open: cin, cout
  assign xor_1_out = Input1 ^ multiplexer_1_out;  // XOR_Gate xor_1, 16 bits wide
  Adder #(.width(5)) adder_16 (.a(adder_14_out), .b(adder_15_out), .out(adder_16_out));  // open: cin, cout
  assign bit_extender_17_out = {{11{1'b0}}, adder_16_out};  // Bit_Extender bit_extender_17
endmodule

module BiClock (
  input  reset,
  output signal0,
  output signal1
);

  wire and_1_out, horloge_out, not_1_out, register_1_q;

  Clock horloge (.out(horloge_out));
  not not_1 (not_1_out, register_1_q);
  Register #(.width(1), .trigger("falling")) register_1 (
    .D(not_1_out), .Q(register_1_q), .clk(horloge_out), .clr(reset));  // open: en
  and and_1 (and_1_out, horloge_out, ~reset);  // AND_Gate
  and and_2 (signal0, ~register_1_q, and_1_out);  // AND_Gate
  and and_3 (signal1, register_1_q, and_1_out);

  // Notes on the sheet:
  //   Ce module divise une horloge en deux sous-horloges alternées
  //   Chronogrammes :
  //   horloge: 0101010101 signal0: 0100010001 signal1: 000100010
  //   registre 1-bit
  //   Enable
  //   select : 0 / 1
endmodule

module DecodeIR (
  input  [15:0] IR,
  output WriteReg,
  output Jump,
  output Load,
  output Store
);

  wire decoder_1_out1, decoder_1_out2, decoder_1_out3, decoder_1_out4, decoder_1_out5, decoder_1_out6,
       decoder_1_out7, decoder_1_out9, decoder_1_out14, or_1_out;
  wire [3:0] undriven;

  Decoder #(.select(4)) decoder_1 (
    .out1(decoder_1_out1), .out2(decoder_1_out2), .out3(decoder_1_out3), .out4(decoder_1_out4),
    .out5(decoder_1_out5), .out6(decoder_1_out6), .out7(decoder_1_out7), .out9(decoder_1_out9), .out12(Jump),
    .out14(decoder_1_out14), .sel(undriven));  // open: out0, out8, out10, out11, out13, out15, en
  or or_1 (or_1_out, decoder_1_out1, decoder_1_out5, decoder_1_out9);
  // Probe on or_1_out
  // OR_Gate or_2 has open pins: in0=decoder_1_out2, in1=decoder_1_out6, out=open
  // OR_Gate or_3 has open pins: in0=decoder_1_out3, in1=decoder_1_out7, out=open
  or or_4 (WriteReg, decoder_1_out1, decoder_1_out2, decoder_1_out4, decoder_1_out5, decoder_1_out6, decoder_1_out9, decoder_1_out14);

  assign Load = Jump;
  assign Store = Jump;
endmodule

module GetAddr (
  input  Fetch,
  input  [15:0] IR,
  input  [15:0] PC,
  input  [15:0] BaseR,
  output [15:0] Addr
);

  wire and_1_out, not_1_out;
  wire [15:0] adder_1_out, adder_2_out, multiplexer_1_out, offset6_1_off6, offset9_1_off9;

  Offset9 offset9_1 (.IR(IR), .Off9(offset9_1_off9));
  Offset6 offset6_1 (.IR(IR), .Off6(offset6_1_off6));
  Adder #(.width(16)) adder_1 (.a(offset6_1_off6), .b(BaseR), .out(adder_1_out));  // open: cin, cout
  Adder #(.width(16)) adder_2 (.a(offset9_1_off9), .b(PC), .out(adder_2_out), .cin(1'b1));  // open: cout
  Multiplexer #(.width(16), .disabled(0), .enable("false")) multiplexer_1 (
    .in0(adder_2_out), .in1(adder_1_out), .out(multiplexer_1_out), .sel(IR[14]));
  not not_1 (not_1_out, Fetch);
  and and_1 (and_1_out, IR[13], not_1_out);
  Multiplexer #(.width(16), .disabled(0), .enable("false")) multiplexer_2 (
    .in0(multiplexer_1_out), .in1(PC), .out(Addr), .sel(and_1_out));

  // Notes on the sheet:
  //   PC+SEXT(Offset6)
  //   PC+SEXT(Offset9)
  //   si Fetch = 1, la porte AND sort 0 = le MUX prend l'entrée 0
  //   Si fetch = 0 et Bit 13 = 1 = la porte AND sort 1 = le MUX prend l'entrée 1
endmodule

module GetCst (
  input  [15:0] IR,
  output [15:0] Cst,
  output UseCst
);

  assign Cst = {{11{IR[4]}}, IR[4:0]};  // Bit_Extender bit_extender_1

  assign UseCst = IR[5];
endmodule

module NZP (
  input  [15:0] RES,
  input  [15:0] IR,
  input  WriteReg,
  output [2:0] NZP,
  output TestNZP
);

  wire and_1_out, and_2_out, and_3_out, clock_1_out, or_1_out;
  wire [2:0] comparator_1_lt, register_1_q;

  Comparator #(.width(16)) comparator_1 (
    .a(RES), .b({16{1'b0}}), .gt(comparator_1_lt[2]), .eq(comparator_1_lt[1]), .lt(comparator_1_lt[0]));
  // NOR_Gate nor_1 has open pins: in0=RES[15], in1=comparator_1_lt[1], out=open
  Register #(.width(3)) register_1 (
    .D(comparator_1_lt), .Q(register_1_q), .clk(clock_1_out), .clr(WriteReg));  // open: en
  Clock clock_1 (.out(clock_1_out));
  and and_1 (and_1_out, register_1_q[2], IR[11]);
  and and_2 (and_2_out, register_1_q[1], IR[11]);
  and and_3 (and_3_out, register_1_q[0], IR[9]);
  or or_1 (or_1_out, and_1_out, and_2_out, and_3_out);

  assign IR[10] = IR[11];
  assign NZP = 3'b000;
  assign TestNZP = 1'b0;
endmodule

// Off6
module Offset6 (
  input  [15:0] IR,
  output [15:0] Off6
);

  assign Off6 = {{10{IR[5]}}, IR[5:0]};  // Bit_Extender bit_extender_1
endmodule

// Off9
module Offset9 (
  input  [15:0] IR,
  output [15:0] Off9
);

  assign Off9 = {{7{IR[8]}}, IR[8:0]};  // Bit_Extender bit_extender_1
endmodule

module Or16 (
  input  [15:0] in_1,
  output out_2
);

  wire [1:0] or_2_out;
  wire [7:0] or_1_out;

  assign or_1_out = in_1[7:0] | in_1[15:8];  // OR_Gate or_1, 8 bits wide
  assign or_2_out = or_1_out[1:0] | or_1_out[3:2] | or_1_out[5:4] | or_1_out[7:6];  // OR_Gate or_2, 2 bits wide
  or or_3 (out_2, or_2_out[0], or_2_out[1]);
endmodule

module RamCtrl (
  input  Exec,
  input  Fetch,
  input  Load,
  input  Store,
  output MemLoad,
  output MemStore
);

  wire and_1_out;

  and and_1 (and_1_out, Exec, Load);
  and and_2 (MemStore, Exec, Store);
  or or_1 (MemLoad, Fetch, and_1_out);
endmodule

module Registres (
  input  [2:0] SR1,
  input  [15:0] IN,
  input  [2:0] SR2,
  input  WriteReg,
  input  [2:0] DR_SR,
  output [15:0] R0,
  output [15:0] OUT_SR1,
  output [15:0] R1,
  output [15:0] R2,
  output [15:0] R3,
  output [15:0] OUT_SR2,
  output [15:0] R4,
  output [15:0] R5,
  output [15:0] OUT_SR,
  output [15:0] R6,
  output [15:0] R7
);

  wire decoder_1_out0, decoder_1_out1, decoder_1_out2, decoder_1_out3, decoder_1_out4, decoder_1_out5,
       decoder_1_out6, decoder_1_out7;

  Decoder #(.select(3), .disabled(0)) decoder_1 (
    .out0(decoder_1_out0), .out1(decoder_1_out1), .out2(decoder_1_out2), .out3(decoder_1_out3),
    .out4(decoder_1_out4), .out5(decoder_1_out5), .out6(decoder_1_out6), .out7(decoder_1_out7), .sel(DR_SR),
    .en(WriteReg));
  Register #(.width(16), .trigger("falling")) u_R0 (.D(IN), .Q(R0), .clk(decoder_1_out0));  // open: en, clr
  Register #(.width(16), .trigger("falling")) u_R1 (.D(IN), .Q(R1), .clk(decoder_1_out1));  // open: en, clr
  Register #(.width(16), .trigger("falling")) u_R2 (.D(IN), .Q(R2), .clk(decoder_1_out2));  // open: en, clr
  Register #(.width(16), .trigger("falling")) u_R3 (.D(IN), .Q(R3), .clk(decoder_1_out3));  // open: en, clr
  Register #(.width(16), .trigger("falling")) u_R4 (.D(IN), .Q(R4), .clk(decoder_1_out4));  // open: en, clr
  Register #(.width(16), .trigger("falling")) u_R5 (.D(IN), .Q(R5), .clk(decoder_1_out5));  // open: en, clr
  Register #(.width(16), .trigger("falling")) u_R6 (.D(IN), .Q(R6), .clk(decoder_1_out6));  // open: en, clr
  Register #(.width(16), .trigger("falling")) u_R7 (.D(IN), .Q(R7), .clk(decoder_1_out7));  // open: en, clr
  Multiplexer #(.select(3), .width(16), .enable("false")) multiplexer_1 (
    .in0(R0), .in1(R1), .in2(R2), .in3(R3), .in4(R4), .in5(R5), .in6(R6), .in7(R7), .out(OUT_SR1), .sel(SR1));
  Multiplexer #(.select(3), .width(16), .enable("false")) multiplexer_2 (
    .in0(R0), .in1(R1), .in2(R2), .in3(R3), .in4(R4), .in5(R5), .in6(R6), .in7(R7), .out(OUT_SR2), .sel(SR2));
  Multiplexer #(.select(3), .width(16), .enable("false")) multiplexer_3 (
    .in0(R0), .in1(R1), .in2(R2), .in3(R3), .in4(R4), .in5(R5), .in6(R6), .in7(R7), .out(OUT_SR), .sel(DR_SR));
endmodule

module RegPC (
  input  [15:0] IR,
  input  H,
  input  [15:0] R,
  input  Reset,
  input  Jump,
  input  TestNZP,
  output [15:0] PC
);

  wire and_1_out, and_2_out, and_3_out, comparator_1_gt, comparator_2_eq, not_1_out, or_1_out, or_2_out;
  wire [15:0] adder_1_out, adder_2_out, bit_extender_1_out, multiplexer_1_out, multiplexer_2_out,
       multiplexer_3_out, offset9_1_off9;

  Offset9 offset9_1 (.IR(IR), .Off9(offset9_1_off9));
  assign bit_extender_1_out = {{5{IR[10]}}, IR[10:0]};  // Bit_Extender bit_extender_1
  Adder #(.width(16)) adder_1 (.a(PC), .b(16'h1), .out(adder_1_out));  // open: cin, cout
  Multiplexer #(.width(16), .disabled(0), .enable("false")) multiplexer_1 (
    .in0(offset9_1_off9), .in1(bit_extender_1_out), .out(multiplexer_1_out), .sel(and_1_out));
  Adder #(.width(16)) adder_2 (.a(adder_1_out), .b(multiplexer_1_out), .out(adder_2_out));  // open: cin, cout
  Comparator #(.width(4)) comparator_1 (.a(IR[15:12]), .b(4'b0000), .gt(comparator_1_gt));  // open: eq, lt
  Multiplexer #(.width(16), .disabled(0), .enable("false")) multiplexer_2 (
    .in0(adder_2_out), .in1(R), .out(multiplexer_2_out), .sel(or_1_out));
  or or_1 (or_1_out, and_1_out, and_2_out);
  Multiplexer #(.width(16), .enable("false")) multiplexer_3 (
    .in0(adder_1_out), .in1(multiplexer_2_out), .out(multiplexer_3_out), .sel(or_2_out));
  or or_2 (or_2_out, Jump, and_3_out);
  and and_1 (and_1_out, comparator_1_gt, TestNZP);
  Register #(.width(16), .trigger("falling")) u_PC (.D(multiplexer_3_out), .Q(PC), .clk(H), .clr(Reset));  // open: en
  not not_1 (not_1_out, IR[11]);
  Comparator #(.width(4)) comparator_2 (.a(IR[15:12]), .b(4'b0100), .eq(comparator_2_eq));  // open: gt, lt
  and and_2 (and_2_out, comparator_2_eq, IR[11]);
  and and_3 (and_3_out, comparator_2_eq, not_1_out);
  // also tied to GND on the sheet: {bit_extender_1_out[0], bit_extender_1_out[1], bit_extender_1_out[2], bit_extender_1_out[3], bit_extender_1_out[4], bit_extender_1_out[5], bit_extender_1_out[6], bit_extender_1_out[7], bit_extender_1_out[8], bit_extender_1_out[9], bit_extender_1_out[10], bit_extender_1_out[11], bit_extender_1_out[12], bit_extender_1_out[13], bit_extender_1_out[14], bit_extender_1_out[15]}

  // Notes on the sheet:
  //   pour BR
  //   pour JSR
  //   PC <- PC + 1
  //   BaseR
  //   PC+Off
  //   pas saut
  //   saut
endmodule

module Offset11 (
  input  [15:0] IR,
  output [15:0] SEXTOff11
);

  assign SEXTOff11 = {{5{1'b0}}, IR[10:0]};  // Bit_Extender bit_extender_1
endmodule

module WriteVal (
  input  [15:0] ALURes,
  input  [15:0] MemOUT,
  input  Load,
  input  [15:0] IR,
  input  [15:0] PC,
  output [15:0] RegIN,
  output [15:0] Off9
);

  wire JSR, LEA;
  wire [15:0] adder_1_out, multiplexer_1_out, multiplexer_2_out, undriven;

  and and_1 (LEA, ~IR[12], IR[13], IR[14], IR[15]);  // AND_Gate
  and and_2 (JSR, ~IR[12], ~IR[13], IR[14], ~IR[15]);  // AND_Gate
  assign Off9 = {{7{IR[8]}}, IR[8:0]};  // Bit_Extender bit_extender_1
  Multiplexer #(.width(16)) multiplexer_1 (
    .in0(ALURes), .in1(MemOUT), .out(multiplexer_1_out), .sel(Load));  // open: en
  Adder #(.width(16)) adder_1 (.a(undriven), .b(PC), .out(adder_1_out));  // open: cin, cout
  Multiplexer #(.width(16)) multiplexer_2 (
    .in0(multiplexer_1_out), .in1(adder_1_out), .out(multiplexer_2_out), .sel(LEA));  // open: en
  Multiplexer #(.width(16)) multiplexer_3 (.in0(multiplexer_2_out), .in1(PC), .out(RegIN), .sel(JSR));  // open: en
endmodule
